// Logisim project D_Flip_Flop.circ as structural Verilog: 1 circuit, main circuit main
module main (
  input  in_1,
  output Q,
  output QBar,
  output out_4,
  output out_5
);

  wire CLK, nand_1_out, nand_2_out, not_1_out;

  Clock clock_1 (.out(CLK));
  not not_1 (not_1_out, in_1);
  nand nand_1 (nand_1_out, in_1, CLK);
  nand nand_2 (nand_2_out, CLK, not_1_out);
  D_Flip_Flop d_ff_1 (.D(in_1), .clk(CLK), .Q(out_4), .Qn(out_5));  // open: preset, reset
  nand nand_3 (Q, nand_1_out, QBar);
  nand nand_4 (QBar, Q, nand_2_out);

  // Other names for the same wires on the sheet: DATA = in_1

  // Notes on the sheet:
  //   D-Flip Flop
endmodule
